# Fritzing sketch sim800L_GSM_Ultrasonic (saved by Fritzing 0.9.3b)
breadboards: 1

parts:
  Part1 = Arduino Nano (Rev3.0)
  GSM_SIM_GPSR_SMS_SIM900_SIM1 = SIM800L [package=THT]
  hc-sr1 = hc-sr04
  R1 = Resistor [tolerance=±5% resistance=220 package="0805 [SMD]"]
  R2 = Resistor [tolerance=±5% resistance=220 package="0805 [SMD]"]
  U1 = BATTERY-2 [package=battery-aa]

nets:
  GND: Part1.GND, hc-sr1.GND
  N1: Part1.D2, R1.Pin_1
  N2: Part1.D3, GSM_SIM_GPSR_SMS_SIM900_SIM1.SIM_TXD
  N3: Part1.D8, hc-sr1.Trig
  N4: Part1.D9, hc-sr1.Echo
  5V: Part1.5V, hc-sr1.VCC
  N5: GSM_SIM_GPSR_SMS_SIM900_SIM1.5V, U1.+1
  N6: GSM_SIM_GPSR_SMS_SIM900_SIM1.GND#1, U1.-1
  N7: GSM_SIM_GPSR_SMS_SIM900_SIM1.SIM_RXD, R1.Pin_0, R2.Pin_1

notes:
  2pcs. - 220 ohm resistor
  1pc. - HC-04 ultrasonic
  1pc. - sim800L GSM
  1pc. - Arduino nano
  3.7V Battery supply to GSM Module
  Wire Color - Connection:
  Black - GND
  Red - VCC
  Blue - D2 to RX
  Yellow - D3 to TX
  Orange - D8 to TrigPin
  Cyan - D9 to EchoPin
  SIM800L GSM Module :: Schematic Diagram
  Made by: Rumil Christian T. Seloveres
  Course: Bachelor of Science in Computer Engineering
